// Logisim project ‏‏single_cycle_mips_6.circ as structural Verilog: 11 circuits, main circuit main
module main (
);

  wire alu_1_zero, and_1_out, ori_1_alusrc, ori_1_branch, ori_1_memread, ori_1_memtoreg, ori_1_memwrite,
       ori_1_regdst, ori_1_regwrite, ori_1_shift, Reset;
  wire [1:0] ori_1_aluop;
  wire [3:0] alu_control_1_out_3;
  wire [4:0] multiplexer_1_out;
  wire [15:0] or_1_out;
  wire [31:0] adder_1_out_3, adder_2_out_3, alu_1_out_5, bit_extender_1_out, data_memory_1_out_5,
       instruction_memory_1_out_2, multiplexer_2_out, multiplexer_3_out, multiplexer_4_out,
       multiplexer_5_out, program_counter_1_out_3, registers_1_read_data_1, registers_1_read_data_2,
       shift_left_2_1_out_2, sign_extend_1_out_2;

  Program_Counter program_counter_1 (.in_1(multiplexer_4_out), .out_3(program_counter_1_out_3), .Reset(Reset));
  Button button_1 (.out(Reset));
  Adder adder_1 (.in_1(program_counter_1_out_3), .in_2(32'h4), .out_3(adder_1_out_3));
  Instruction_Memory instruction_memory_1 (
    .in_1(program_counter_1_out_3),
    .out_2({instruction_memory_1_out_2[31:4], or_1_out[2], instruction_memory_1_out_2[2:0]}));
  Multiplexer #(.width(5), .enable("false")) multiplexer_1 (
    .in0(instruction_memory_1_out_2[20:16]), .in1(instruction_memory_1_out_2[15:11]),
    .out(multiplexer_1_out), .sel(ori_1_regdst));
  Registers registers_1 (
    .Read_1_Address(instruction_memory_1_out_2[25:21]), .Read_2_Address(instruction_memory_1_out_2[20:16]),
    .Write_Address(multiplexer_1_out), .Write_Data(multiplexer_3_out), .Write_Enable(ori_1_regwrite),
    .Read_Data_1(registers_1_read_data_1), .Read_Data_2(registers_1_read_data_2), .Reset(Reset));
  ori ori_1 (
    .RegDst(ori_1_regdst), .ALUSrc(ori_1_alusrc), .MemToReg(ori_1_memtoreg), .RegWrite(ori_1_regwrite),
    .MemRead(ori_1_memread), .MemWrite(ori_1_memwrite), .Branch(ori_1_branch), .ALUOp(ori_1_aluop),
    .in_1(instruction_memory_1_out_2[31:26]), .Shift(ori_1_shift));
  Sign_Extend sign_extend_1 (
    .in_1({instruction_memory_1_out_2[15:4], or_1_out[2], instruction_memory_1_out_2[2:0]}),
    .out_2(sign_extend_1_out_2));
  Multiplexer #(.width(32), .enable("false")) multiplexer_2 (
    .in0(registers_1_read_data_2), .in1(sign_extend_1_out_2), .out(multiplexer_2_out), .sel(ori_1_alusrc));
  Multiplexer #(.width(32), .enable("false")) multiplexer_3 (
    .in0(multiplexer_5_out), .in1(bit_extender_1_out), .out(multiplexer_3_out), .sel(ori_1_shift));
  Shift_Left_2 shift_left_2_1 (.in_1(sign_extend_1_out_2), .out_2(shift_left_2_1_out_2));
  ALU_Control alu_control_1 (
    .in_1(ori_1_aluop), .out_3(alu_control_1_out_3),
    .in_2({instruction_memory_1_out_2[5:4], or_1_out[2], instruction_memory_1_out_2[2:0]}));
  ALU alu_1 (
    .in_1(registers_1_read_data_1), .in_2(multiplexer_2_out), .in_3(alu_control_1_out_3), .Zero(alu_1_zero),
    .out_5(alu_1_out_5));
  or or_1 (or_1_out[0], registers_1_read_data_1[0], instruction_memory_1_out_2[0]);
  Adder adder_2 (.in_1(adder_1_out_3), .in_2(shift_left_2_1_out_2), .out_3(adder_2_out_3));
  and and_1 (and_1_out, ori_1_branch, alu_1_zero);
  or or_2 (or_1_out[1], registers_1_read_data_1[1], instruction_memory_1_out_2[1]);
  or or_3 (or_1_out[2], registers_1_read_data_1[2], instruction_memory_1_out_2[2]);
  Multiplexer #(.width(32), .enable("false")) multiplexer_4 (
    .in0(adder_1_out_3), .in1(adder_2_out_3), .out(multiplexer_4_out), .sel(and_1_out));
  or or_4 (or_1_out[3], registers_1_read_data_1[3], or_1_out[2]);
  Data_Memory data_memory_1 (
    .in_2(alu_1_out_5), .MemRead(ori_1_memread), .out_5(data_memory_1_out_5), .MemWrite(ori_1_memwrite),
    .in_3(registers_1_read_data_2));
  or or_5 (or_1_out[4], registers_1_read_data_1[4], instruction_memory_1_out_2[4]);
  Multiplexer #(.width(32), .enable("false")) multiplexer_5 (
    .in0(alu_1_out_5), .in1(data_memory_1_out_5), .out(multiplexer_5_out), .sel(ori_1_memtoreg));
  or or_6 (or_1_out[5], registers_1_read_data_1[5], instruction_memory_1_out_2[5]);
  or or_7 (or_1_out[6], registers_1_read_data_1[6], instruction_memory_1_out_2[6]);
  or or_8 (or_1_out[7], registers_1_read_data_1[7], instruction_memory_1_out_2[7]);
  or or_9 (or_1_out[8], registers_1_read_data_1[8], instruction_memory_1_out_2[8]);
  or or_10 (or_1_out[10], registers_1_read_data_1[10], instruction_memory_1_out_2[10]);
  or or_11 (or_1_out[9], registers_1_read_data_1[9], instruction_memory_1_out_2[9]);
  or or_12 (or_1_out[11], registers_1_read_data_1[11], instruction_memory_1_out_2[11]);
  or or_13 (or_1_out[12], registers_1_read_data_1[12], instruction_memory_1_out_2[12]);
  or or_14 (or_1_out[13], registers_1_read_data_1[13], instruction_memory_1_out_2[13]);
  or or_15 (or_1_out[14], registers_1_read_data_1[14], instruction_memory_1_out_2[14]);
  or or_16 (or_1_out[15], registers_1_read_data_1[15], instruction_memory_1_out_2[15]);
  assign bit_extender_1_out = {{16{1'b0}}, or_1_out};  // Bit_Extender bit_extender_1
endmodule

module Registers (
  input  [4:0] Read_1_Address,
  input  [4:0] Read_2_Address,
  input  [4:0] Write_Address,
  input  [31:0] Write_Data,
  input  Write_Enable,
  input  Reset,
  output [31:0] Read_Data_1,
  output [31:0] Read_Data_2
);

  wire and_1_out, and_2_out, and_3_out, and_4_out, and_5_out, and_6_out, and_7_out, and_8_out, and_9_out,
       and_10_out, and_11_out, and_12_out, and_13_out, and_14_out, and_15_out, and_16_out, and_17_out,
       and_18_out, and_19_out, and_20_out, and_21_out, and_22_out, and_23_out, and_24_out, and_25_out,
       and_26_out, and_27_out, and_28_out, and_29_out, and_30_out, and_31_out, and_32_out, Clock_out,
       decoder_1_out0, decoder_1_out1, decoder_1_out2, decoder_1_out3, decoder_1_out4, decoder_1_out5,
       decoder_1_out6, decoder_1_out7, decoder_1_out8, decoder_1_out9, decoder_1_out10, decoder_1_out11,
       decoder_1_out12, decoder_1_out13, decoder_1_out14, decoder_1_out15, decoder_1_out16, decoder_1_out17,
       decoder_1_out18, decoder_1_out19, decoder_1_out20, decoder_1_out21, decoder_1_out22, decoder_1_out23,
       decoder_1_out24, decoder_1_out25, decoder_1_out26, decoder_1_out27, decoder_1_out28, decoder_1_out29,
       decoder_1_out30, decoder_1_out31;
  wire [31:0] multiplexer_1_out, multiplexer_2_out, multiplexer_3_out, multiplexer_4_out, register_2_q,
       register_3_q, register_4_q, register_5_q, register_6_q, register_7_q, register_8_q, register_9_q,
       register_10_q, register_11_q, register_12_q, register_13_q, register_14_q, register_15_q,
       register_16_q, register_17_q, register_18_q, register_19_q, register_20_q, register_21_q,
       register_22_q, register_23_q, register_24_q, register_25_q, register_26_q, register_27_q,
       register_28_q, register_29_q, register_30_q, register_31_q, register_32_q;

  Decoder #(.select(5), .enable("false")) decoder_1 (
    .out0(decoder_1_out0), .out1(decoder_1_out1), .out2(decoder_1_out2), .out3(decoder_1_out3),
    .out4(decoder_1_out4), .out5(decoder_1_out5), .out6(decoder_1_out6), .out7(decoder_1_out7),
    .out8(decoder_1_out8), .out9(decoder_1_out9), .out10(decoder_1_out10), .out11(decoder_1_out11),
    .out12(decoder_1_out12), .out13(decoder_1_out13), .out14(decoder_1_out14), .out15(decoder_1_out15),
    .out16(decoder_1_out16), .out17(decoder_1_out17), .out18(decoder_1_out18), .out19(decoder_1_out19),
    .out20(decoder_1_out20), .out21(decoder_1_out21), .out22(decoder_1_out22), .out23(decoder_1_out23),
    .out24(decoder_1_out24), .out25(decoder_1_out25), .out26(decoder_1_out26), .out27(decoder_1_out27),
    .out28(decoder_1_out28), .out29(decoder_1_out29), .out30(decoder_1_out30), .out31(decoder_1_out31),
    .sel(Write_Address));
  Clock Clock (.out(Clock_out));
  and and_1 (and_1_out, decoder_1_out0, Write_Enable);
  and and_2 (and_2_out, decoder_1_out1, Write_Enable);
  and and_3 (and_3_out, decoder_1_out2, Write_Enable);
  and and_4 (and_4_out, decoder_1_out3, Write_Enable);
  and and_5 (and_5_out, decoder_1_out4, Write_Enable);
  and and_6 (and_6_out, decoder_1_out5, Write_Enable);
  and and_7 (and_7_out, decoder_1_out6, Write_Enable);
  and and_8 (and_8_out, decoder_1_out7, Write_Enable);
  and and_9 (and_9_out, decoder_1_out8, Write_Enable);
  and and_10 (and_10_out, decoder_1_out9, Write_Enable);
  and and_11 (and_11_out, decoder_1_out10, Write_Enable);
  and and_12 (and_12_out, decoder_1_out11, Write_Enable);
  and and_13 (and_13_out, decoder_1_out12, Write_Enable);
  and and_14 (and_14_out, decoder_1_out13, Write_Enable);
  and and_15 (and_15_out, decoder_1_out14, Write_Enable);
  and and_16 (and_16_out, decoder_1_out15, Write_Enable);
  and and_17 (and_17_out, decoder_1_out16, Write_Enable);
  and and_18 (and_18_out, decoder_1_out17, Write_Enable);
  and and_19 (and_19_out, decoder_1_out18, Write_Enable);
  and and_20 (and_20_out, decoder_1_out19, Write_Enable);
  and and_21 (and_21_out, decoder_1_out20, Write_Enable);
  and and_22 (and_22_out, decoder_1_out21, Write_Enable);
  and and_23 (and_23_out, decoder_1_out22, Write_Enable);
  and and_24 (and_24_out, decoder_1_out23, Write_Enable);
  and and_25 (and_25_out, decoder_1_out24, Write_Enable);
  and and_26 (and_26_out, decoder_1_out25, Write_Enable);
  and and_27 (and_27_out, decoder_1_out26, Write_Enable);
  and and_28 (and_28_out, decoder_1_out27, Write_Enable);
  and and_29 (and_29_out, decoder_1_out28, Write_Enable);
  and and_30 (and_30_out, decoder_1_out29, Write_Enable);
  and and_31 (and_31_out, decoder_1_out30, Write_Enable);
  and and_32 (and_32_out, decoder_1_out31, Write_Enable);
  Register #(.width(32)) register_1 (.D(Write_Data), .en(and_1_out), .clk(Clock_out));  // open: Q, clr
  Register #(.width(32)) register_2 (.D(Write_Data), .en(and_2_out), .Q(register_2_q), .clk(Clock_out), .clr(Reset));
  Register #(.width(32)) register_3 (.D(Write_Data), .en(and_3_out), .Q(register_3_q), .clk(Clock_out), .clr(Reset));
  Register #(.width(32)) register_4 (.D(Write_Data), .en(and_4_out), .Q(register_4_q), .clk(Clock_out), .clr(Reset));
  Register #(.width(32)) register_5 (.D(Write_Data), .en(and_5_out), .Q(register_5_q), .clk(Clock_out), .clr(Reset));
  Register #(.width(32)) register_6 (.D(Write_Data), .en(and_6_out), .Q(register_6_q), .clk(Clock_out), .clr(Reset));
  Register #(.width(32)) register_7 (.D(Write_Data), .en(and_7_out), .Q(register_7_q), .clk(Clock_out), .clr(Reset));
  Register #(.width(32)) register_8 (.D(Write_Data), .en(and_8_out), .Q(register_8_q), .clk(Clock_out), .clr(Reset));
  Register #(.width(32)) register_9 (.D(Write_Data), .en(and_9_out), .Q(register_9_q), .clk(Clock_out), .clr(Reset));
  Register #(.width(32)) register_10 (.D(Write_Data), .en(and_10_out), .Q(register_10_q), .clk(Clock_out), .clr(Reset));
  Register #(.width(32)) register_11 (.D(Write_Data), .en(and_11_out), .Q(register_11_q), .clk(Clock_out), .clr(Reset));
  Register #(.width(32)) register_12 (.D(Write_Data), .en(and_12_out), .Q(register_12_q), .clk(Clock_out), .clr(Reset));
  Register #(.width(32)) register_13 (.D(Write_Data), .en(and_13_out), .Q(register_13_q), .clk(Clock_out), .clr(Reset));
  Register #(.width(32)) register_14 (.D(Write_Data), .en(and_14_out), .Q(register_14_q), .clk(Clock_out), .clr(Reset));
  Register #(.width(32)) register_15 (.D(Write_Data), .en(and_15_out), .Q(register_15_q), .clk(Clock_out), .clr(Reset));
  Register #(.width(32)) register_16 (.D(Write_Data), .en(and_16_out), .Q(register_16_q), .clk(Clock_out), .clr(Reset));
  Register #(.width(32)) register_17 (.D(Write_Data), .en(and_17_out), .Q(register_17_q), .clk(Clock_out), .clr(Reset));
  Register #(.width(32)) register_18 (.D(Write_Data), .en(and_18_out), .Q(register_18_q), .clk(Clock_out), .clr(Reset));
  Register #(.width(32)) register_19 (.D(Write_Data), .en(and_19_out), .Q(register_19_q), .clk(Clock_out), .clr(Reset));
  Register #(.width(32)) register_20 (.D(Write_Data), .en(and_20_out), .Q(register_20_q), .clk(Clock_out), .clr(Reset));
  Register #(.width(32)) register_21 (.D(Write_Data), .en(and_21_out), .Q(register_21_q), .clk(Clock_out), .clr(Reset));
  Register #(.width(32)) register_22 (.D(Write_Data), .en(and_22_out), .Q(register_22_q), .clk(Clock_out), .clr(Reset));
  Register #(.width(32)) register_23 (.D(Write_Data), .en(and_23_out), .Q(register_23_q), .clk(Clock_out), .clr(Reset));
  Register #(.width(32)) register_24 (.D(Write_Data), .en(and_24_out), .Q(register_24_q), .clk(Clock_out), .clr(Reset));
  Register #(.width(32)) register_25 (.D(Write_Data), .en(and_25_out), .Q(register_25_q), .clk(Clock_out), .clr(Reset));
  Register #(.width(32)) register_26 (.D(Write_Data), .en(and_26_out), .Q(register_26_q), .clk(Clock_out), .clr(Reset));
  Register #(.width(32)) register_27 (.D(Write_Data), .en(and_27_out), .Q(register_27_q), .clk(Clock_out), .clr(Reset));
  Register #(.width(32)) register_28 (.D(Write_Data), .en(and_28_out), .Q(register_28_q), .clk(Clock_out), .clr(Reset));
  Register #(.width(32)) register_29 (.D(Write_Data), .en(and_29_out), .Q(register_29_q), .clk(Clock_out), .clr(Reset));
  Register #(.width(32)) register_30 (.D(Write_Data), .en(and_30_out), .Q(register_30_q), .clk(Clock_out), .clr(Reset));
  Register #(.width(32)) register_31 (.D(Write_Data), .en(and_31_out), .Q(register_31_q), .clk(Clock_out), .clr(Reset));
  Register #(.width(32)) register_32 (.D(Write_Data), .en(and_32_out), .Q(register_32_q), .clk(Clock_out), .clr(Reset));
  Multiplexer #(.select(4), .width(32), .enable("false")) multiplexer_1 (
    .in0({32{1'b0}}), .in1(register_2_q), .in2(register_3_q), .in3(register_4_q), .in4(register_5_q),
    .in5(register_6_q), .in6(register_7_q), .in7(register_8_q), .in8(register_9_q), .in9(register_10_q),
    .in10(register_11_q), .in11(register_12_q), .in12(register_13_q), .in13(register_14_q),
    .in14(register_15_q), .in15(register_16_q), .out(multiplexer_1_out), .sel(Read_2_Address[3:0]));
  Multiplexer #(.select(4), .width(32), .enable("false")) multiplexer_2 (
    .in0({32{1'b0}}), .in1(register_2_q), .in2(register_3_q), .in3(register_4_q), .in4(register_5_q),
    .in5(register_6_q), .in6(register_7_q), .in7(register_8_q), .in8(register_9_q), .in9(register_10_q),
    .in10(register_11_q), .in11(register_12_q), .in12(register_13_q), .in13(register_14_q),
    .in14(register_15_q), .in15(register_16_q), .out(multiplexer_2_out), .sel(Read_1_Address[3:0]));
  Multiplexer #(.select(4), .width(32), .enable("false")) multiplexer_3 (
    .in0(register_17_q), .in1(register_18_q), .in2(register_19_q), .in3(register_20_q), .in4(register_21_q),
    .in5(register_22_q), .in6(register_23_q), .in7(register_24_q), .in8(register_25_q), .in9(register_26_q),
    .in10(register_27_q), .in11(register_28_q), .in12(register_29_q), .in13(register_30_q),
    .in14(register_31_q), .in15(register_32_q), .out(multiplexer_3_out), .sel(Read_1_Address[3:0]));
  Multiplexer #(.select(4), .width(32), .enable("false")) multiplexer_4 (
    .in0(register_17_q), .in1(register_18_q), .in2(register_19_q), .in3(register_20_q), .in4(register_21_q),
    .in5(register_22_q), .in6(register_23_q), .in7(register_24_q), .in8(register_25_q), .in9(register_26_q),
    .in10(register_27_q), .in11(register_28_q), .in12(register_29_q), .in13(register_30_q),
    .in14(register_31_q), .in15(register_32_q), .out(multiplexer_4_out), .sel(Read_2_Address[3:0]));
  Multiplexer #(.width(32), .enable("false")) multiplexer_5 (
    .in0(multiplexer_2_out), .in1(multiplexer_3_out), .out(Read_Data_1), .sel(Read_1_Address[4]));
  Multiplexer #(.width(32), .enable("false")) multiplexer_6 (
    .in0(multiplexer_1_out), .in1(multiplexer_4_out), .out(Read_Data_2), .sel(Read_2_Address[4]));
endmodule

module ALU (
  input  [31:0] in_1,
  input  [31:0] in_2,
  input  [3:0] in_3,
  output Zero,
  output [31:0] out_5
);

  wire or_2_out, or_3_out, or_4_out, or_5_out, or_6_out;
  wire [31:0] adder_1_out, and_1_out, nor_1_out, or_1_out, subtractor_1_out;

  assign and_1_out = in_1 & in_2;  // AND_Gate and_1, 32 bits wide
  assign or_1_out = in_1 | in_2;  // OR_Gate or_1, 32 bits wide
  Adder_part #(.width(32)) adder_1 (.a(in_1), .b(in_2), .out(adder_1_out));  // open: cin, cout
  Subtractor #(.width(32)) subtractor_1 (.a(in_1), .b(in_2), .out(subtractor_1_out));  // open: bin, bout
  assign nor_1_out = ~(in_1 | in_2);  // NOR_Gate nor_1, 32 bits wide
  Multiplexer #(.select(4), .width(32), .enable("false")) multiplexer_1 (
    .in0(and_1_out), .in1(or_1_out), .in2(adder_1_out), .in6(subtractor_1_out),
    .in7({{31{1'b0}}, subtractor_1_out[31]}), .in12(nor_1_out), .out(out_5), .sel(in_3));  // open: in3, in4, in5, in8, in9, in10, in11, in13, in14, in15
  or or_2 (or_2_out, out_5[0], out_5[1], out_5[2], out_5[3], out_5[4], out_5[5], out_5[6], out_5[7], out_5[8]);
  or or_3 (or_3_out, out_5[9], out_5[10], out_5[11], out_5[12], out_5[13], out_5[14], out_5[15], out_5[16], out_5[17]);
  or or_4 (or_4_out, out_5[18], out_5[19], out_5[20], out_5[21], out_5[22], out_5[23], out_5[24], out_5[25], out_5[26]);
  or or_5 (or_5_out, out_5[27], out_5[28], out_5[29], out_5[30], out_5[31]);
  or or_6 (or_6_out, or_2_out, or_3_out, or_4_out, or_5_out);
  not not_1 (Zero, or_6_out);
endmodule

module Instruction_Memory (
  input  [31:0] in_1,
  output [31:0] out_2
);

  wire clock_1_out;

  Clock clock_1 (.out(clock_1_out));
  RAM #(.addrWidth(24), .dataWidth(32), .bus("separate")) ram_1 (
    .addr(in_1[23:0]), .data(out_2), .str(1'b0), .sel(1'b1), .clk(clock_1_out), .ld(1'b1));  // open: din, clr
endmodule

module Program_Counter (
  input  [31:0] in_1,
  input  Reset,
  output [31:0] out_3
);

  wire clock_1_out;

  Register #(.width(32)) register_1 (.D(in_1), .en(1'b1), .Q(out_3), .clk(clock_1_out), .clr(Reset));
  Clock clock_1 (.out(clock_1_out));
endmodule

module Sign_Extend (
  input  [15:0] in_1,
  output [31:0] out_2
);


  assign out_2 = {{17{in_1[15]}}, in_1[14:0]};
endmodule

module Data_Memory (
  input  MemWrite,
  input  [31:0] in_2,
  input  [31:0] in_3,
  input  MemRead,
  output [31:0] out_5
);

  wire clock_1_out;

  Clock clock_1 (.out(clock_1_out));
  RAM #(.addrWidth(24), .dataWidth(32), .bus("separate")) ram_1 (
    .addr(in_2[23:0]), .din(in_3), .data(out_5), .str(MemWrite), .sel(1'b1), .clk(clock_1_out), .ld(MemRead),
    .clr(1'b0));
endmodule

module Shift_Left_2 (
  input  [31:0] in_1,
  output [31:0] out_2
);


  assign out_2 = {in_1[29:0], 2'b00};
endmodule

module Adder (
  input  [31:0] in_1,
  input  [31:0] in_2,
  output [31:0] out_3
);

  ALU alu_1 (.in_1(in_1), .in_2(in_2), .in_3(4'b0010), .out_5(out_3));  // open: Zero
endmodule

module ALU_Control (
  input  [1:0] in_1,
  input  [5:0] in_2,
  output [3:0] out_3
);

  wire [3:0] multiplexer_1_out;

  Multiplexer #(.select(4), .width(4), .enable("false")) multiplexer_1 (
    .in0(4'b0010), .in2(4'b0110), .in4(4'b0000), .in5(4'b0001), .in10(4'b0111), .out(multiplexer_1_out),
    .sel(in_2[3:0]));  // open: in1, in3, in6, in7, in8, in9, in11, in12, in13, in14, in15
  Multiplexer #(.select(2), .width(4), .enable("false")) multiplexer_2 (
    .in0(4'b0010), .in1(4'b0110), .in2(multiplexer_1_out), .out(out_3), .sel(in_1));  // open: in3

  // Notes on the sheet:
  //   Instruction [5-0]
endmodule

module ori (
  input  [5:0] in_1,
  output RegDst,
  output ALUSrc,
  output MemToReg,
  output RegWrite,
  output MemRead,
  output MemWrite,
  output Branch,
  output [1:0] ALUOp,
  output Shift
);

  and and_1 (ALUOp[1], ~in_1[5], ~in_1[4], ~in_1[3], ~in_1[2], ~in_1[1], ~in_1[0]);  // AND_Gate
  and and_2 (MemRead, in_1[5], ~in_1[4], ~in_1[3], ~in_1[2], in_1[1], in_1[0]);  // AND_Gate
  and and_3 (MemWrite, in_1[5], ~in_1[4], in_1[3], ~in_1[2], in_1[1], in_1[0]);  // AND_Gate
  and and_4 (ALUOp[0], ~in_1[5], ~in_1[4], ~in_1[3], in_1[2], ~in_1[1], ~in_1[0]);  // AND_Gate
  and and_5 (MemRead, ~in_1[5], ~in_1[4], ~in_1[3], in_1[2], ~in_1[1], ~in_1[0]);  // AND_Gate
  or or_1 (ALUSrc, MemRead, MemWrite);
  or or_2 (RegWrite, ALUOp[1], MemRead, MemRead);

  assign Branch = ALUOp[0];
  assign MemToReg = MemRead;
  assign RegDst = ALUOp[1];
  assign Shift = MemRead;

  // Notes on the sheet:
  //   R-Format
  //   lw
  //   sw
  //   beq
  //   ori
endmodule
